# Fritzing sketch clock_with_ir_led (saved by Fritzing 0.9.3b)
breadboards: 1

parts:
  Arduino_Nano = Arduino Nano (Rev3.0)
  NPN-Transistor = NPN-Transistor [package="TO92 [THT]"]
  Infrared_LED = LED - 5mm [color="Infrared (850nm)" package="5 mm [THT]"]
  DS3231_RTC = ZS-042 RTC Module
  Digit_Display = Grove 4 Digit Display
  Power_Jack = Power Jack [package=power_jack_smd]
  R1 = Resistor [tolerance=±5% resistance=10k package=THT]
  R2 = Resistor [tolerance=±5% resistance=10k package=THT]
  R3 = Resistor [tolerance=±5% resistance=10k package=THT]
  S1 = Pushbutton [package="[THT]"]
  S2 = Pushbutton [package="[THT]"]
  S3 = Pushbutton [package="[THT]"]
  DHT1 = DHT11 Humitidy and Temperature Sensor

nets:
  GND: Arduino_Nano.GND, Infrared_LED.cathode, DS3231_RTC.GND, Digit_Display.GND, Power_Jack.GND, R1.Pin_0, R2.Pin_0, R3.Pin_0, DHT1.GND
  N1: Arduino_Nano.D2, R2.Pin_1, S3.Pin_3
  N2: Arduino_Nano.D3, NPN-Transistor.B
  N3: Arduino_Nano.D4, DHT1.DATA
  N4: Arduino_Nano.D5, R1.Pin_1, S2.Pin_3, S2.Pin_4
  N5: Arduino_Nano.D6, R3.Pin_1, S1.Pin_3
  N6: Arduino_Nano.D7, Digit_Display.DIO
  N7: Arduino_Nano.D8, Digit_Display.CLK
  N8: Arduino_Nano.VIN, Power_Jack.GNDBREAK
  VCC: Arduino_Nano.5V, NPN-Transistor.C, DS3231_RTC.VCC, Digit_Display.VCC, S1.Pin_1, S2.Pin_1, S2.Pin_2, S3.Pin_1, DHT1.VDD
  N9: Arduino_Nano.A5, DS3231_RTC.SCL
  N10: Arduino_Nano.A4, DS3231_RTC.SDA
  N11: NPN-Transistor.E, Infrared_LED.anode

custom parts:
  DHT11 Humitidy and Temperature Sensor: DHT11 Humidity and Temperature Sensor
